// Logisim project Projeto.circ as structural Verilog: 6 circuits, main circuit Main
module Main (
  input  in_1
);

  wire clk, cont_dados, cont_reg, DadosUla_mux, mux_ula;
  wire [1:0] cont_ula;
  wire [2:0] bint_1_code, r1, r2;
  wire [8:0] DadosUla_Reg, imm, memdados_1_d_out, multiplexer_1_out, rx_add, ry_data, ula_1_s0;

  Clock u_CLK (.out(clk));
  BInt bint_1 (.CLK(clk), .zera(in_1), .R2_y(r2), .R1_x(r1), .code(bint_1_code), .imm(imm));
  un_contr un_contr_1 (
    .Sel_inst(bint_1_code), .mux_ula(mux_ula), .cont_dados(cont_dados), .cont_reg(cont_reg),
    .DadosUla_mux(DadosUla_mux), .Cont_ULA(cont_ula));
  banco_reg banco_reg_1 (
    .E_dados(DadosUla_Reg), .W(cont_reg), .CLK(clk), .Rx_select(r1), .Ry_select(r2), .Sel_reg(r1),
    .Rx(rx_add), .Ry(ry_data));
  Multiplexer #(.width(9)) multiplexer_1 (.in0(ry_data), .in1(imm), .out(multiplexer_1_out), .sel(mux_ula));
  Multiplexer #(.width(9)) multiplexer_2 (
    .in0(ula_1_s0), .in1(memdados_1_d_out), .out(DadosUla_Reg), .sel(DadosUla_mux));
  ULA ula_1 (.E0(rx_add), .E1(multiplexer_1_out), .operacao(cont_ula), .S0(ula_1_s0));
  MemDados memdados_1 (.CLK(clk), .W(cont_dados), .D_In(ry_data), .Adress(rx_add), .D_Out(memdados_1_d_out));

  // Notes on the sheet:
  //   imm/r2
  //   r1
endmodule

module BInt (
  input  CLK,
  input  zera,
  output [2:0] R2_y,
  output [2:0] R1_x,
  output [2:0] code,
  output [8:0] imm
);

  wire [4:0] add, reg_instrucoes_q;

  Register #(.width(5)) reg_instrucoes (.D(add), .en(1'b1), .clk(CLK), .Q(reg_instrucoes_q), .clr(zera));
  ROM #(.addrWidth(5), .dataWidth(9)) Bint (.addr(reg_instrucoes_q), .data({code, R1_x, R2_y}));
  Adder #(.width(5)) adder_1 (.a(reg_instrucoes_q), .b(5'b00001), .out(add));  // open: cin, cout
  assign imm = {{6{R2_y[2]}}, R2_y};  // Bit_Extender bit_extender_1

  // Notes on the sheet:
  //   contents of Bint (hex, n*v repeats v):
  //   0 10b 181 10b 189
endmodule

module banco_reg (
  input  [8:0] E_dados,
  input  W,
  input  CLK,
  input  [2:0] Rx_select,
  input  [2:0] Ry_select,
  input  [2:0] Sel_reg,
  output [8:0] Rx,
  output [8:0] Ry
);

  wire and1, and2, and3, and4, and5, and6, and7, sl1, sl2, sl3, sl4, sl5, sl6, sl7;
  wire [8:0] s1, s2, s3, s4, s5, s6, s7;

  Decoder #(.select(3)) decoder_1 (
    .out1(and1), .out2(and2), .out3(and3), .out4(and4), .out5(and5), .out6(and6), .out7(and7), .sel(Sel_reg));  // open: out0, en
  and and_1 (sl1, W, and1);
  and and_2 (sl5, W, and5);
  Register #(.width(9)) R2 (.D(E_dados), .en(sl2), .clk(CLK), .Q(s2));  // open: clr
  Register #(.width(9)) R4 (.D(E_dados), .en(sl4), .clk(CLK), .Q(s4));  // open: clr
  Register #(.width(9)) R6 (.D(E_dados), .en(sl6), .clk(CLK), .Q(s6));  // open: clr
  and and_3 (sl2, W, and2);
  and and_4 (sl6, W, and6);
  and and_5 (sl3, W, and3);
  and and_6 (sl7, W, and7);
  Register #(.width(9)) R1 (.D(E_dados), .en(sl1), .clk(CLK), .Q(s1));  // open: clr
  Register #(.width(9)) R3 (.D(E_dados), .en(sl3), .clk(CLK), .Q(s3));  // open: clr
  Register #(.width(9)) R5 (.D(E_dados), .en(sl5), .clk(CLK), .Q(s5));  // open: clr
  Register #(.width(9)) R7 (.D(E_dados), .en(sl7), .clk(CLK), .Q(s7));  // open: clr
  and and_7 (sl4, W, and4);
  Multiplexer #(.select(3), .width(9)) multiplexer_1 (
    .in0({9{1'b0}}), .in1(s1), .in2(s2), .in3(s3), .in4(s4), .in5(s5), .in6(s6), .in7(s7), .out(Rx),
    .sel(Rx_select));
  Multiplexer #(.select(3), .width(9)) multiplexer_2 (
    .in0({9{1'b0}}), .in1(s1), .in2(s2), .in3(s3), .in4(s4), .in5(s5), .in6(s6), .in7(s7), .out(Ry),
    .sel(Ry_select));

  // Other names for the same wires on the sheet: e_d[8:0] = E_dados

  // Notes on the sheet:
  //   R0
endmodule

module ULA (
  input  [8:0] E0,
  input  [8:0] E1,
  input  [1:0] operacao,
  output [8:0] S0
);

  wire comparador_1_p3;
  wire [8:0] adder_1_out, bit_extender_1_out, multiplier_1_out, subtractor_1_out;

  // comparador comparador_1: pin names not known; wires that end beside it: E0, E1, comparador_1_p3
  Adder #(.width(9)) adder_1 (.a(E0), .b(E1), .out(adder_1_out));  // open: cin, cout
  Subtractor #(.width(9)) subtractor_1 (.a(E0), .b(E1), .out(subtractor_1_out));  // open: bin, bout
  Multiplier #(.mode("twosComplement"), .width(9)) multiplier_1 (
    .a(E0), .b(E1), .out(multiplier_1_out));  // open: cin, cout
  assign bit_extender_1_out = {{8{1'b0}}, comparador_1_p3};  // Bit_Extender bit_extender_1
  Multiplexer #(.select(2), .width(9)) multiplexer_1 (
    .in0(adder_1_out), .in1(subtractor_1_out), .in2(multiplier_1_out), .in3(bit_extender_1_out), .out(S0),
    .sel(operacao));
endmodule

module MemDados (
  input  CLK,
  input  W,
  input  [8:0] D_In,
  input  [8:0] Adress,
  output [8:0] D_Out
);

  RAM #(.addrWidth(9), .dataWidth(9)) ram_1 (.addr(Adress), .we(W), .oe(1'b1), .clk(CLK), .din(D_In), .dout(D_Out));

  // Other names for the same wires on the sheet: ADR[8:0] = Adress; DATA_IN[8:0] = D_In; DATA_OUT[8:0] = D_Out;
  //   WR = W
endmodule

module un_contr (
  input  [2:0] Sel_inst,
  output mux_ula,
  output cont_dados,
  output cont_reg,
  output DadosUla_mux,
  output [1:0] Cont_ULA
);

  ROM #(.addrWidth(3), .dataWidth(6)) rom_1 (
    .addr(Sel_inst), .data({mux_ula, cont_dados, cont_reg, DadosUla_mux, Cont_ULA}));

  // Notes on the sheet:
  //   contents of rom_1 (hex, n*v repeats v):
  //   8 9 a b 28 c 10
endmodule
